// Logisim project cpu.circ as structural Verilog: 5 circuits, main circuit main
module main (
  input  [31:0] INSTRUCTION,
  input  CLOCK,
  output [31:0] PROGRAM_COUNTER,
  output [31:0] ra,
  output [31:0] sp,
  output [31:0] t0,
  output [31:0] t1,
  output [31:0] t2,
  output [31:0] s0,
  output [31:0] s1,
  output [31:0] a0
);

  wire DMEM_p1, DMEM_p3;
  wire [2:0] funct3;
  wire [6:0] funct7;
  wire [24:0] INSTRUCTION_STAGE2;
  wire [31:0] adder_1_out, alu_result, read_data1, read_data2;

  Adder #(.width(32)) adder_1 (.a(PROGRAM_COUNTER), .b(32'h4), .out(adder_1_out));  // open: cin, cout
  Register #(.width(32)) register_1 (
    .D(INSTRUCTION), .en(1'b1), .clk(CLOCK),
    .Q({funct7, INSTRUCTION_STAGE2[24:15], funct3, INSTRUCTION_STAGE2[11:0]}));  // open: clr
  Register #(.width(32)) PC (.D(adder_1_out), .clk(CLOCK), .Q(PROGRAM_COUNTER));  // open: en, clr
  // controls contrl: pin names not known; wires that end beside it: {funct7, INSTRUCTION_STAGE2[24:15], funct3, INSTRUCTION_STAGE2[11:0]}
  immediate_generation imm_gen (.in_1({funct7, INSTRUCTION_STAGE2[24:15], funct3, INSTRUCTION_STAGE2[11:0]}));  // open: out_2
  alu Arithmetic_Logic_Unit (.A(read_data1), .Result(alu_result));  // open: ALUSel, B, out_5, out_6
  regfile_main RegFile (
    .rs2(INSTRUCTION_STAGE2[24:20]), .rd(INSTRUCTION_STAGE2[11:7]), .Read_Data_1(read_data1),
    .Read_Data_2(read_data2), .ra(ra), .sp(sp), .t0(t0), .t1(t1), .t2(t2), .s0(s0), .s1(s1), .a0(a0),
    .rs1(INSTRUCTION_STAGE2[19:15]), .clk(CLOCK));  // open: Write_Data, RegWEn
  // mem_main DMEM: pin names not known; wires that end beside it: DMEM_p1, DMEM_p1, DMEM_p3

  // Other names for the same wires on the sheet: clk = CLOCK; opcode[6:0] = INSTRUCTION_STAGE2[6:0];
  //   rd[4:0] = INSTRUCTION_STAGE2[11:7]; INSTRUCTION_STAGE2 (some bits) = {funct7, funct3};
  //   rs1[4:0] = INSTRUCTION_STAGE2[19:15]; rs2[4:0] = INSTRUCTION_STAGE2[24:20]

  // Notes on the sheet:
  //   Output
  //   IMEM (do **NOT** move this)
  //   Inputs
  //   It is OK to move the PC, RegFile, ALU, and MEM to wherever is most convenient for you when constructing your CPU, and to delete this text
  //   Inputs/Outputs for testing. Do **NOT** move these.
endmodule

module instruction_decoder (
  input  [31:0] in_1
);


  // Other names for the same wires on the sheet: INSTRUCTION[31:0] = in_1
endmodule

module controls (
  input  [31:0] in_1,
  output MemRW,
  output RegWEn,
  output MemToReg,
  output ALUSrc,
  output Branch,
  output ALUOp0,
  output ALUOp1
);

  OpcodeTo3Bit opcodeto3bit_1 ();  // open: Opcode, Bit0, Bit1, Bit2

  // Other names for the same wires on the sheet: INSTRUCTION[31:0] = in_1
endmodule

module immediate_generation (
  input  [31:0] in_1,
  output [31:0] out_2
);

  wire bit0, bit1, bit2;
  wire [31:0] bit_extender_4_out, I_IMM, S_IMM, SB_IMM, U_IMM, UJ_IMM;

  assign I_IMM = {{20{in_1[31]}}, in_1[31:20]};  // Bit_Extender bit_extender_1
  assign S_IMM = {{20{in_1[31]}}, {in_1[31:25], in_1[11:7]}};  // Bit_Extender bit_extender_2
  assign U_IMM = {{12{in_1[31]}}, in_1[31:12]};  // Bit_Extender bit_extender_3
  assign bit_extender_4_out = {{20{in_1[31]}}, {in_1[31], in_1[7], in_1[30:25], in_1[11:8]}};  // Bit_Extender bit_extender_4
  assign UJ_IMM = {{12{in_1[31]}}, {in_1[31], in_1[19:12], in_1[20], in_1[30:21]}};  // Bit_Extender bit_extender_5
  Shifter #(.width(32)) shifter_1 (.in(bit_extender_4_out), .out(SB_IMM));  // open: dist
  OpcodeTo3Bit opcodeto3bit_1 (.Opcode(in_1[6:0]), .Bit0(bit0), .Bit1(bit1), .Bit2(bit2));
  Multiplexer #(.select(3), .width(32), .enable("false")) multiplexer_1 (
    .in0({32{1'b0}}), .in1(I_IMM), .in2(S_IMM), .in3(SB_IMM), .in4(U_IMM), .in5(UJ_IMM), .in6({32{1'b0}}),
    .in7({32{1'b0}}), .out(out_2), .sel({bit2, bit1, bit0}));

  // Other names for the same wires on the sheet: INSTRUCTION[31:0] = in_1; rd[4:0] = in_1[11:7];
  //   imm[11:0] = in_1[31:20]; func3[2:0] = in_1[14:12]; rs1[4:0] = in_1[19:15]; opcode[6:0] = in_1[6:0]
endmodule

module OpcodeTo3Bit (
  input  [6:0] Opcode,
  output Bit0,
  output Bit1,
  output Bit2
);

  wire not_1_out, not_2_out, not_3_out, not_4_out, not_5_out, not_6_out, O1, O2, O3, O4, O5, O6;
  wire [6:0] and_1_out, and_2_out, and_3_out, and_4_out, and_5_out, and_10_out, and_11_out, and_12_out,
       or_1_out;

  assign and_1_out = Opcode & 7'b0110011;  // AND_Gate and_1, 7 bits wide
  assign and_2_out = Opcode & 7'b0100011;  // AND_Gate and_2, 7 bits wide
  assign and_3_out = Opcode & 7'b1100011;  // AND_Gate and_3, 7 bits wide
  assign and_4_out = Opcode & 7'b0110111;  // AND_Gate and_4, 7 bits wide
  assign and_5_out = Opcode & 7'b1101111;  // AND_Gate and_5, 7 bits wide
  and and_6 (O4, and_3_out[0], and_3_out[1], and_3_out[2], and_3_out[3], and_3_out[4], and_3_out[5], and_3_out[6]);
  and and_7 (O5, and_4_out[0], and_4_out[1], and_4_out[2], and_4_out[3], and_4_out[4], and_4_out[5], and_4_out[6]);
  and and_8 (O6, and_5_out[0], and_5_out[1], and_5_out[2], and_5_out[3], and_5_out[4], and_5_out[5], and_5_out[6]);
  and and_9 (O1, and_1_out[0], and_1_out[1], and_1_out[2], and_1_out[3], and_1_out[4], and_1_out[5], and_1_out[6]);
  assign and_10_out = Opcode & 7'b0000011;  // AND_Gate and_10, 7 bits wide
  assign and_11_out = Opcode & 7'b0010011;  // AND_Gate and_11, 7 bits wide
  assign and_12_out = Opcode & 7'b1100111;  // AND_Gate and_12, 7 bits wide
  and and_13 (O3, and_2_out[0], and_2_out[1], and_2_out[2], and_2_out[3], and_2_out[4], and_2_out[5], and_2_out[6]);
  assign or_1_out = and_10_out | and_11_out | and_12_out;  // OR_Gate or_1, 7 bits wide
  and and_14 (O2, or_1_out[0], or_1_out[1], or_1_out[2], or_1_out[3], or_1_out[4], or_1_out[5], or_1_out[6]);
  not not_1 (not_1_out, O1);
  not not_2 (not_2_out, O2);
  not not_3 (not_3_out, O3);
  not not_4 (not_4_out, O4);
  not not_5 (not_5_out, O5);
  not not_6 (not_6_out, O6);
  or or_2 (Bit0, O2, O4, O6);
  or or_3 (Bit1, O3, O4);
  or or_4 (Bit2, O5, O6);
endmodule
