// Logisim project regfile.circ as structural Verilog: 1 circuit, main circuit main
module main (
  input  [4:0] rs1,
  input  [4:0] rs2,
  input  [4:0] rd,
  input  [31:0] Write_Data,
  input  RegWEn,
  input  clk,
  output [31:0] ra,
  output [31:0] sp,
  output [31:0] t0,
  output [31:0] t1,
  output [31:0] t2,
  output [31:0] s0,
  output [31:0] s1,
  output [31:0] a0,
  output [31:0] Read_Data_1,
  output [31:0] Read_Data_2
);

  wire [31:0] demultiplexer_1_out9, x0_input, x0_output, x1_input, x2_input, x5_input, x6_input, x7_input,
       x8_input, x9_input, x10_input;

  Register #(.width(32)) x0 (.D(x0_input), .en(1'b0), .clk(clk), .Q(x0_output));  // open: clr
  Register #(.width(32)) x7 (.D(x7_input), .en(RegWEn), .clk(clk), .Q(t2));  // open: clr
  Multiplexer #(.select(5), .width(32), .enable("false")) multiplexer_1 (
    .in0(x0_output), .in1(ra), .in2(sp), .in3(t0), .in4(t1), .in5(t2), .in6(s0), .in7(s1), .in8(a0),
    .in9({32{1'b0}}), .in10({32{1'b0}}), .in11({32{1'b0}}), .in12({32{1'b0}}), .in13({32{1'b0}}),
    .in14({32{1'b0}}), .in15({32{1'b0}}), .in16({32{1'b0}}), .in17({32{1'b0}}), .in18({32{1'b0}}),
    .in19({32{1'b0}}), .in20({32{1'b0}}), .in21({32{1'b0}}), .in22({32{1'b0}}), .in23({32{1'b0}}),
    .in24({32{1'b0}}), .in25({32{1'b0}}), .in26({32{1'b0}}), .in27({32{1'b0}}), .in28({32{1'b0}}),
    .in29({32{1'b0}}), .in30({32{1'b0}}), .out(Read_Data_1), .sel(rs1));  // open: in31
  Multiplexer #(.select(5), .width(32), .enable("false")) multiplexer_2 (
    .in0(x0_output), .in1(ra), .in2(sp), .in3(t0), .in4(t1), .in5(t2), .in6(s0), .in7(s1), .in8(a0),
    .in9({32{1'b0}}), .in10({32{1'b0}}), .in11({32{1'b0}}), .in12({32{1'b0}}), .in13({32{1'b0}}),
    .in14({32{1'b0}}), .in15({32{1'b0}}), .in16({32{1'b0}}), .in17({32{1'b0}}), .in18({32{1'b0}}),
    .in19({32{1'b0}}), .in20({32{1'b0}}), .in21({32{1'b0}}), .in22({32{1'b0}}), .in23({32{1'b0}}),
    .in24({32{1'b0}}), .in25({32{1'b0}}), .in26({32{1'b0}}), .in27({32{1'b0}}), .in28({32{1'b0}}),
    .in29({32{1'b0}}), .in30({32{1'b0}}), .in31({32{1'b0}}), .out(Read_Data_2), .sel(rs2));
  Register #(.width(32)) x1 (.D(x1_input), .en(RegWEn), .clk(clk), .Q(ra));  // open: clr
  Demultiplexer #(.select(5), .width(32), .enable("false")) demultiplexer_1 (
    .out0(x0_input), .out1(x1_input), .out2(x2_input), .out3(x5_input), .out4(x6_input), .out5(x7_input),
    .out6(x8_input), .out7(x9_input), .out8(x10_input), .out9(demultiplexer_1_out9),
    .out10(demultiplexer_1_out9), .out11(demultiplexer_1_out9), .out12(demultiplexer_1_out9),
    .out13(demultiplexer_1_out9), .out14(demultiplexer_1_out9), .out15(demultiplexer_1_out9),
    .out16(demultiplexer_1_out9), .out17(demultiplexer_1_out9), .out18(demultiplexer_1_out9),
    .out19(demultiplexer_1_out9), .out20(demultiplexer_1_out9), .out21(demultiplexer_1_out9),
    .out22(demultiplexer_1_out9), .out23(demultiplexer_1_out9), .out24(demultiplexer_1_out9),
    .out25(demultiplexer_1_out9), .out26(demultiplexer_1_out9), .out27(demultiplexer_1_out9),
    .out28(demultiplexer_1_out9), .out29(demultiplexer_1_out9), .out30(demultiplexer_1_out9),
    .out31(demultiplexer_1_out9), .in(Write_Data), .sel(rd));
  Register #(.width(32)) x2 (.D(x2_input), .en(RegWEn), .clk(clk), .Q(sp));  // open: clr
  Register #(.width(32)) x8 (.D(x8_input), .en(RegWEn), .clk(clk), .Q(s0));  // open: clr
  Register #(.width(32)) x5 (.D(x5_input), .en(RegWEn), .clk(clk), .Q(t0));  // open: clr
  Register #(.width(32)) x9 (.D(x9_input), .en(RegWEn), .clk(clk), .Q(s1));  // open: clr
  Register #(.width(32)) x6 (.D(x6_input), .en(RegWEn), .clk(clk), .Q(t1));  // open: clr
  Register #(.width(32)) x10 (.D(x10_input), .en(RegWEn), .clk(clk), .Q(a0));  // open: clr
  // also tied to GND on the sheet: {demultiplexer_1_out9[0], demultiplexer_1_out9[1], demultiplexer_1_out9[2], demultiplexer_1_out9[3], demultiplexer_1_out9[4], demultiplexer_1_out9[5], demultiplexer_1_out9[6], demultiplexer_1_out9[7], demultiplexer_1_out9[8], demultiplexer_1_out9[9], demultiplexer_1_out9[10], demultiplexer_1_out9[11], demultiplexer_1_out9[12], demultiplexer_1_out9[13], demultiplexer_1_out9[14], demultiplexer_1_out9[15], demultiplexer_1_out9[16], demultiplexer_1_out9[17], demultiplexer_1_out9[18], demultiplexer_1_out9[19], demultiplexer_1_out9[20], demultiplexer_1_out9[21], demultiplexer_1_out9[22], demultiplexer_1_out9[23], demultiplexer_1_out9[24], demultiplexer_1_out9[25], demultiplexer_1_out9[26], demultiplexer_1_out9[27], demultiplexer_1_out9[28], demultiplexer_1_out9[29], demultiplexer_1_out9[30], demultiplexer_1_out9[31]}

  // Other names for the same wires on the sheet: read_data1[31:0] = Read_Data_1; read_data2[31:0] = Read_Data_2;
  //   read_reg1[4:0] = rs1; read_reg2[4:0] = rs2; write_en = RegWEn; write_reg[4:0] = rd; x1_output[31:0] = ra;
  //   x2_output[31:0] = sp; x5_output[31:0] = t0; x6_output[31:0] = t1; x7_output[31:0] = t2; x8_output[31:0] = s0;
  //   x9_output[31:0] = s1; x10_output[31:0] = a0

  // Notes on the sheet:
  //   INPUTS to your circuit
  //   DON'T CHANGE THE LOCATIONS OF THE INPUTS AND OUTPUTS!
  //   These are DEBUG/TEST outputs from your circuit.
  //   OUTPUTS from your circuit
endmodule
